// Logisim project adder.circ as structural Verilog: 2 circuits, main circuit main
module main (
  input  [15:0] B,
  input  [15:0] A,
  input  sub,
  output [15:0] Result,
  output ovf
);

  wire n1_bit_adder_1_c_out, n1_bit_adder_2_c_out, n1_bit_adder_3_c_out, n1_bit_adder_4_c_out,
       n1_bit_adder_5_c_out, n1_bit_adder_6_c_out, n1_bit_adder_7_c_out, n1_bit_adder_8_c_out,
       n1_bit_adder_9_c_out, n1_bit_adder_10_c_out, n1_bit_adder_11_c_out, n1_bit_adder_12_c_out,
       n1_bit_adder_13_c_out, n1_bit_adder_14_c_out, n1_bit_adder_15_c_out, n1_bit_adder_16_c_out, xor_2_out,
       xor_3_out, xor_4_out, xor_5_out, xor_6_out, xor_7_out, xor_8_out, xor_9_out, xor_10_out, xor_11_out,
       xor_12_out, xor_13_out, xor_14_out, xor_15_out, xor_16_out, xor_17_out;

  xor xor_1 (ovf, n1_bit_adder_1_c_out, n1_bit_adder_2_c_out);
  _1_bit_Adder u_1_bit_adder_1 (
    .A(xor_2_out), .B(B[15]), .C_in(n1_bit_adder_2_c_out), .C_out(n1_bit_adder_1_c_out), .Sum(Result[15]));
  _1_bit_Adder u_1_bit_adder_2 (
    .A(xor_3_out), .B(B[14]), .C_in(n1_bit_adder_3_c_out), .C_out(n1_bit_adder_2_c_out), .Sum(Result[14]));
  xor xor_2 (xor_2_out, sub, A[15]);
  _1_bit_Adder u_1_bit_adder_3 (
    .A(xor_4_out), .B(B[13]), .C_in(n1_bit_adder_4_c_out), .C_out(n1_bit_adder_3_c_out), .Sum(Result[13]));
  xor xor_3 (xor_3_out, sub, A[14]);
  xor xor_4 (xor_4_out, sub, A[13]);
  _1_bit_Adder u_1_bit_adder_4 (
    .A(xor_5_out), .B(B[12]), .C_in(n1_bit_adder_5_c_out), .C_out(n1_bit_adder_4_c_out), .Sum(Result[12]));
  xor xor_5 (xor_5_out, sub, A[12]);
  _1_bit_Adder u_1_bit_adder_5 (
    .A(xor_6_out), .B(B[11]), .C_in(n1_bit_adder_6_c_out), .C_out(n1_bit_adder_5_c_out), .Sum(Result[11]));
  xor xor_6 (xor_6_out, sub, A[11]);
  _1_bit_Adder u_1_bit_adder_6 (
    .A(xor_7_out), .B(B[10]), .C_in(n1_bit_adder_7_c_out), .C_out(n1_bit_adder_6_c_out), .Sum(Result[10]));
  xor xor_7 (xor_7_out, sub, A[10]);
  _1_bit_Adder u_1_bit_adder_7 (
    .A(xor_8_out), .B(B[9]), .C_in(n1_bit_adder_9_c_out), .C_out(n1_bit_adder_7_c_out), .Sum(Result[9]));
  xor xor_8 (xor_8_out, sub, A[9]);
  _1_bit_Adder u_1_bit_adder_8 (
    .A(xor_10_out), .B(B[7]), .C_in(n1_bit_adder_10_c_out), .C_out(n1_bit_adder_8_c_out), .Sum(Result[7]));
  _1_bit_Adder u_1_bit_adder_9 (
    .A(xor_9_out), .B(B[8]), .C_in(n1_bit_adder_8_c_out), .C_out(n1_bit_adder_9_c_out), .Sum(Result[8]));
  xor xor_9 (xor_9_out, sub, A[8]);
  _1_bit_Adder u_1_bit_adder_10 (
    .A(xor_12_out), .B(B[6]), .C_in(n1_bit_adder_11_c_out), .C_out(n1_bit_adder_10_c_out), .Sum(Result[6]));
  xor xor_10 (xor_10_out, sub, A[7]);
  _1_bit_Adder u_1_bit_adder_11 (
    .A(xor_11_out), .B(B[5]), .C_in(n1_bit_adder_12_c_out), .C_out(n1_bit_adder_11_c_out), .Sum(Result[5]));
  xor xor_11 (xor_11_out, sub, A[5]);
  xor xor_12 (xor_12_out, sub, A[6]);
  _1_bit_Adder u_1_bit_adder_12 (
    .A(xor_13_out), .B(B[4]), .C_in(n1_bit_adder_13_c_out), .C_out(n1_bit_adder_12_c_out), .Sum(Result[4]));
  xor xor_13 (xor_13_out, sub, A[4]);
  _1_bit_Adder u_1_bit_adder_13 (
    .A(xor_14_out), .B(B[3]), .C_in(n1_bit_adder_14_c_out), .C_out(n1_bit_adder_13_c_out), .Sum(Result[3]));
  xor xor_14 (xor_14_out, sub, A[3]);
  _1_bit_Adder u_1_bit_adder_14 (
    .A(xor_15_out), .B(B[2]), .C_in(n1_bit_adder_15_c_out), .C_out(n1_bit_adder_14_c_out), .Sum(Result[2]));
  xor xor_15 (xor_15_out, sub, A[2]);
  _1_bit_Adder u_1_bit_adder_15 (
    .A(xor_16_out), .B(B[1]), .C_in(n1_bit_adder_16_c_out), .C_out(n1_bit_adder_15_c_out), .Sum(Result[1]));
  xor xor_16 (xor_16_out, sub, A[1]);
  _1_bit_Adder u_1_bit_adder_16 (.A(xor_17_out), .B(B[0]), .C_in(sub), .C_out(n1_bit_adder_16_c_out), .Sum(Result[0]));
  xor xor_17 (xor_17_out, sub, A[0]);

  // Other names for the same wires on the sheet: a00 = A[0]; a01 = A[1]; a02 = A[2]; a03 = A[3]; a04 = A[4];
  //   a05 = A[5]; a06 = A[6]; a07 = A[7]; a08 = A[8]; a09 = A[9]; b00 = B[0]; b01 = B[1]; b02 = B[2]; b03 = B[3];
  //   b04 = B[4]; b05 = B[5]; b06 = B[6]; b07 = B[7]; b08 = B[8]; b09 = B[9]
endmodule

module _1_bit_Adder (
  input  A,
  input  B,
  input  C_in,
  output C_out,
  output Sum
);

  wire and_1_out, and_2_out, xor_1_out;

  and and_1 (and_1_out, A, B);
  xor xor_1 (xor_1_out, A, B);
  and and_2 (and_2_out, xor_1_out, C_in);
  or or_1 (C_out, and_1_out, and_2_out);
  xor xor_2 (Sum, xor_1_out, C_in);
endmodule
