// Logisim project circuit1c.circ as structural Verilog: 1 circuit, main circuit main
module main (
  input  A,
  input  B,
  input  C,
  output out_4,
  output out_5
);

  wire and_1_out, and_2_out, and_3_out, and_4_out, Opposite_A, Opposite_B, Opposite_C;

  not not_1 (Opposite_A, A);
  not not_2 (Opposite_B, B);
  not not_3 (Opposite_C, C);
  and and_1 (and_1_out, A, B);
  and and_2 (and_2_out, Opposite_A, Opposite_B, Opposite_C);
  and and_3 (and_3_out, A, Opposite_C);
  and and_4 (and_4_out, Opposite_A, C);
  or or_1 (out_5, and_1_out, and_2_out);
  or or_2 (out_4, and_3_out, and_4_out, B);

  // Other names for the same wires on the sheet: Same_A = A; Same_B = B; Same_C = C
endmodule
