// Logisim project fsm.circ as structural Verilog: 1 circuit, main circuit main
module main (
  input  in2,
  input  in1,
  output out
);

  wire and_1_out, and_2_out, and_3_out, and_4_out, and_5_out, and_7_out, clock_1_out, diff, not_2_out,
       not_3_out, NOTQD1, NOTQD2, or_1_out, or_2_out, QD1, QD2, same;

  and and_1 (and_1_out, NOTQD1, QD2);
  and and_2 (and_2_out, NOTQD1, NOTQD2);
  xor xor_1 (diff, in2, in1);
  or or_1 (or_1_out, and_1_out, and_2_out);
  not not_1 (same, diff);
  and and_3 (and_3_out, same, or_1_out);
  Clock clock_1 (.out(clock_1_out));
  D_Flip_Flop D1 (.D(not_2_out), .clk(clock_1_out), .Q(QD1), .Qn(NOTQD1));  // open: preset, reset
  not not_2 (not_2_out, and_3_out);
  and and_4 (and_4_out, NOTQD2, QD1);
  and and_5 (and_5_out, NOTQD2, NOTQD1);
  or or_2 (or_2_out, and_4_out, and_5_out);
  and and_6 (out, QD1, QD2);
  and and_7 (and_7_out, diff, or_2_out);
  D_Flip_Flop D2 (.D(not_3_out), .clk(clock_1_out), .Q(QD2), .Qn(NOTQD2));  // open: preset, reset
  not not_3 (not_3_out, and_7_out);
endmodule
